// Digital circuit ALU.dig as structural Verilog
module ALU (
  input  [63:0] A,
  input  [63:0] B,
  input  [3:0] ALUOp,
  output [63:0] R
);

  wire [63:0] add_1_s, and_1_out, div_1_q, mul_1_mul, or_1_out, SLL_out, SRA_out, SRL_out, sub_1_s, xor_1_out;

  Add #(.Bits(64)) add_1 (.a(A), .b(B), .c_i(1'b0), .s(add_1_s));  // open: c_o
  Sub #(.Bits(64)) sub_1 (.a(A), .b(B), .c_i(1'b0), .s(sub_1_s));  // open: c_o
  Mul #(.Signed("true"), .Bits(32)) mul_1 (.a(A[31:0]), .b(B[31:0]), .mul(mul_1_mul));
  BarrelShifter #(.Bits(64)) SLL (.in(A), .shift(B[6:0]), .out(SLL_out));
  BarrelShifter #(.Bits(64), .direction("right")) SRL (.in(A), .shift(B[6:0]), .out(SRL_out));
  assign and_1_out = A & B;  // And and_1, 64 bits wide
  assign or_1_out = A | B;  // Or or_1, 64 bits wide
  assign xor_1_out = A ^ B;  // XOr xor_1, 64 bits wide
  BarrelShifter #(.Bits(64), .barrelShifterMode("arithmetic"), .barrelSigned("true"), .direction("right")) SRA (
    .in(A), .shift(B[7:0]), .out(SRA_out));
  Div #(.Bits(64), .Signed("true")) div_1 (.a(A), .b(B), .q(div_1_q));  // open: r
  Multiplexer #(.Selector_Bits(4), .Bits(64)) multiplexer_1 (
    .sel(ALUOp), .in_0(add_1_s), .in_1(sub_1_s), .in_2(mul_1_mul), .in_3(SLL_out), .in_4(SRL_out),
    .in_5(and_1_out), .in_6(or_1_out), .in_7(xor_1_out), .in_8(SRA_out), .in_9(div_1_q), .in_10({64{1'b0}}),
    .in_11({64{1'b0}}), .in_12({64{1'b0}}), .in_13({64{1'b0}}), .in_14({64{1'b0}}), .in_15({64{1'b0}}),
    .out(R));
endmodule
