// Digital circuit BU.dig as structural Verilog
module BU (
  input  [63:0] A,
  input  [63:0] B,
  input  [1:0] BRop,
  output BR
);

  wire beq_eq, bge_eq, bge_gt, blt_lt, bne_eq, not_1_out, or_1_out;

  Comparator #(.Bits(64)) beq (.a(A), .b(B), .eq(beq_eq));  // open: gt, lt
  Comparator #(.Bits(64)) bne (.a(A), .b(B), .eq(bne_eq));  // open: gt, lt
  Comparator #(.Bits(64)) blt (.a(A), .b(B), .lt(blt_lt));  // open: gt, eq
  Comparator #(.Bits(64)) bge (.a(A), .b(B), .gt(bge_gt), .eq(bge_eq));  // open: lt
  not not_1 (not_1_out, bne_eq);
  or or_1 (or_1_out, bge_gt, bge_eq);
  Multiplexer #(.Selector_Bits(2)) multiplexer_1 (
    .sel(BRop), .in_0(beq_eq), .in_1(not_1_out), .in_2(blt_lt), .in_3(or_1_out), .out(BR));
endmodule
