// Digital circuit InstDecoder.dig as structural Verilog
module InstDecoder (
  input  [31:0] IW,
  output [2:0] ALUSrcB,
  output ALUSrcA,
  output [3:0] ALUOp,
  output RFW,
  output [1:0] WDsel,
  output [1:0] PCsel,
  output [1:0] BROp,
  output Store,
  output [1:0] Msz,
  output [4:0] INUM,
  output Load
);

  wire add_i_1_eq, add_r_1_eq, and_1_eq, beq_1_eq, bge_1_eq, blt_1_eq, bne_1_eq, div_1_eq, jal_1_eq,
       jalr_1_p3, lb_1_eq, lbu_1_eq, ld_1_eq, lw_1_eq, mul_1_eq, or_1_eq, sb_1_eq, sd_1_eq, sll_1_eq,
       slli_1_eq, sra_1_eq, srl_1_eq, srli_1_eq, sub_1_eq, sw_1_eq, xor_1_eq;

  add_i add_i_1 (.opcode(IW[6:0]), .funct3(IW[14:12]), .eq(add_i_1_eq));
  add_r add_r_1 (.opcode(IW[6:0]), .funct3(IW[14:12]), .funct7(IW[31:25]), .eq(add_r_1_eq));
  jal jal_1 (.opcode(IW[6:0]), .eq(jal_1_eq));
  // jalr jalr_1: pin names not known; wires that end beside it: IW[6:0], IW[14:12], jalr_1_p3
  mul mul_1 (.opcode(IW[6:0]), .funct3(IW[14:12]), .funct7(IW[31:25]), .eq(mul_1_eq));
  sll sll_1 (.opcode(IW[6:0]), .funct3(IW[14:12]), .funct7(IW[31:25]), .eq(sll_1_eq));
  slli slli_1 (.opcode(IW[6:0]), .funct3(IW[14:12]), .funct6(IW[31:26]), .eq(slli_1_eq));
  srl srl_1 (.opcode(IW[6:0]), .funct3(IW[14:12]), .funct7(IW[31:25]), .eq(srl_1_eq));
  srli srli_1 (.opcode(IW[6:0]), .funct3(IW[14:12]), .funct6(IW[31:26]), .eq(srli_1_eq));
  beq beq_1 (.opcode(IW[6:0]), .funct3(IW[14:12]), .eq(beq_1_eq));
  bne bne_1 (.opcode(IW[6:0]), .funct3(IW[14:12]), .eq(bne_1_eq));
  blt blt_1 (.opcode(IW[6:0]), .funct3(IW[14:12]), .eq(blt_1_eq));
  bge bge_1 (.opcode(IW[6:0]), .funct3(IW[14:12]), .eq(bge_1_eq));
  sub sub_1 (.opcode(IW[6:0]), .funct3(IW[14:12]), .funct7(IW[31:25]), .eq(sub_1_eq));
  \and  and_1 (.opcode(IW[6:0]), .funct3(IW[14:12]), .funct7(IW[31:25]), .eq(and_1_eq));
  ld ld_1 (.opcode(IW[6:0]), .funct3(IW[14:12]), .eq(ld_1_eq));
  lw lw_1 (.opcode(IW[6:0]), .funct3(IW[14:12]), .eq(lw_1_eq));
  lb lb_1 (.opcode(IW[6:0]), .funct3(IW[14:12]), .eq(lb_1_eq));
  sd sd_1 (.opcode(IW[6:0]), .funct3(IW[14:12]), .eq(sd_1_eq));
  sw sw_1 (.opcode(IW[6:0]), .funct3(IW[14:12]), .eq(sw_1_eq));
  sb sb_1 (.opcode(IW[6:0]), .funct3(IW[14:12]), .eq(sb_1_eq));
  \or  or_1 (.opcode(IW[6:0]), .funct3(IW[14:12]), .funct7(IW[31:25]), .eq(or_1_eq));
  lbu lbu_1 (.opcode(IW[6:0]), .funct3(IW[14:12]), .eq(lbu_1_eq));
  \xor  xor_1 (.opcode(IW[6:0]), .funct3(IW[14:12]), .funct7(IW[31:25]), .eq(xor_1_eq));
  sra sra_1 (.opcode(IW[6:0]), .funct3(IW[14:12]), .funct7(IW[31:25]), .eq(sra_1_eq));
  div div_1 (.opcode(IW[6:0]), .funct3(IW[14:12]), .funct7(IW[31:25]), .eq(div_1_eq));
  PriorityEncoder #(.Selector_Bits(5)) priorityencoder_1 (
    .in0(add_i_1_eq), .in1(add_r_1_eq), .in2(jal_1_eq), .in3(jalr_1_p3), .in4(mul_1_eq), .in5(sll_1_eq),
    .in6(slli_1_eq), .in7(srl_1_eq), .in8(srli_1_eq), .in9(beq_1_eq), .in10(bne_1_eq), .in11(blt_1_eq),
    .in12(bge_1_eq), .in13(sub_1_eq), .in14(and_1_eq), .in15(ld_1_eq), .in16(lw_1_eq), .in17(lb_1_eq),
    .in18(sd_1_eq), .in19(sw_1_eq), .in20(sb_1_eq), .in21(or_1_eq), .in22(lbu_1_eq), .in23(xor_1_eq),
    .in24(sra_1_eq), .in25(div_1_eq), .in26(1'b0), .in27(1'b0), .in28(1'b0), .in29(1'b0), .in30(1'b0),
    .in31(1'b0), .num(INUM));  // open: any
  ROM #(.AddrBits(5), .Bits(19)) rom_1 (
    .A(INUM), .sel(1'b1), .D({Msz, Load, Store, BROp, RFW, ALUOp, ALUSrcA, ALUSrcB, PCsel, WDsel}));

  // Other names for the same wires on the sheet: opcode[6:0] = IW[6:0]; funct3[2:0] = IW[14:12];
  //   funct7[6:0] = IW[31:25]; funct6[5:0] = IW[31:26]

  // Notes on the sheet:
  //   contents of rom_1 (hex, n*v repeats v):
  //   1010,1000,10a5,1015,1200,1300,1310,1400,1410,b9,20b9,40b9,60b9
  //   ,1100,1500,71012,51012,11012,68040,58040,18040,1600,1003,1700
  //   ,1800,1900
endmodule
