// Digital circuit add-i.dig as structural Verilog
module add_i (
  input  [6:0] opcode,
  input  [2:0] funct3,
  output eq
);

  wire add_eq, i_type_eq;

  Comparator #(.Bits(7)) i_type (.a(opcode), .b(7'b0010011), .eq(i_type_eq));  // open: gt, lt
  Comparator #(.Bits(3)) add (.a(funct3), .b(3'b000), .eq(add_eq));  // open: gt, lt
  and and_1 (eq, i_type_eq, add_eq);
endmodule
