// Digital circuit bge.dig as structural Verilog
module bge (
  input  [6:0] opcode,
  input  [2:0] funct3,
  output eq
);

  wire bge_eq, r_type_eq;

  Comparator #(.Bits(7)) r_type (.a(opcode), .b(7'b1100011), .eq(r_type_eq));  // open: gt, lt
  Comparator #(.Bits(3)) bge (.a(funct3), .b(3'b101), .eq(bge_eq));  // open: gt, lt
  and and_1 (eq, r_type_eq, bge_eq);
endmodule
