// Digital circuit blt.dig as structural Verilog
module blt (
  input  [6:0] opcode,
  input  [2:0] funct3,
  output eq
);

  wire blt_eq, r_type_eq;

  Comparator #(.Bits(7)) r_type (.a(opcode), .b(7'b1100011), .eq(r_type_eq));  // open: gt, lt
  Comparator #(.Bits(3)) blt (.a(funct3), .b(3'b100), .eq(blt_eq));  // open: gt, lt
  and and_1 (eq, r_type_eq, blt_eq);
endmodule
