// Digital circuit div.dig as structural Verilog
module div (
  input  [6:0] opcode,
  input  [2:0] funct3,
  input  [6:0] funct7,
  output eq
);

  wire mul_2_eq, mul_eq, r_type_eq;

  Comparator #(.Bits(7)) r_type (.a(opcode), .b(7'b0110011), .eq(r_type_eq));  // open: gt, lt
  Comparator #(.Bits(3)) mul (.a(funct3), .b(3'b100), .eq(mul_eq));  // open: gt, lt
  Comparator #(.Bits(7)) mul_2 (.a(funct7), .b(7'b0000001), .eq(mul_2_eq));  // open: gt, lt
  and and_1 (eq, r_type_eq, mul_eq, mul_2_eq);
endmodule
