// Digital circuit jalr.dig as structural Verilog
module jalr (
  input  [6:0] opcode,
  input  [2:0] funct3,
  output eq
);

  wire i_type_jalr_eq, jalr_eq;

  Comparator #(.Bits(7)) i_type_jalr (.a(opcode), .b(7'b1100111), .eq(i_type_jalr_eq));  // open: gt, lt
  Comparator #(.Bits(3)) jalr (.a(funct3), .b(3'b000), .eq(jalr_eq));  // open: gt, lt
  and and_1 (eq, i_type_jalr_eq, jalr_eq);
  // Pins of 1 and 3 bits meet at funct3
endmodule
