// Digital circuit lb-decoder.dig as structural Verilog
module lb_decoder (
  input  [63:0] D,
  input  [2:0] offset,
  output [63:0] Dlb
);

  wire [7:0] multiplexer_1_out;

  Multiplexer #(.Selector_Bits(3), .Bits(8)) multiplexer_1 (
    .sel(offset), .in_0(D[7:0]), .in_1(D[15:8]), .in_2(D[23:16]), .in_3(D[31:24]), .in_4(D[39:32]),
    .in_5(D[47:40]), .in_6(D[55:48]), .in_7(D[63:56]), .out(multiplexer_1_out));
  BitExtender #(.outputBits(64)) bitextender_1 (.in(multiplexer_1_out), .out(Dlb));
endmodule
