// Digital circuit lbu.dig as structural Verilog
module lbu (
  input  [6:0] opcode,
  input  [2:0] funct3,
  output eq
);

  wire funct3_eq, r_type_eq;

  Comparator #(.Bits(7)) r_type (.a(opcode), .b(7'b0000011), .eq(r_type_eq));  // open: gt, lt
  Comparator #(.Bits(3)) u_funct3 (.a(funct3), .b(3'b100), .eq(funct3_eq));  // open: gt, lt
  and and_1 (eq, r_type_eq, funct3_eq);
endmodule
