// Digital circuit lw-decoder.dig as structural Verilog
module lw_decoder (
  input  [63:0] D,
  input  offset,
  output [63:0] Dlw
);

  wire [31:0] multiplexer_1_out;

  Multiplexer #(.Bits(32)) multiplexer_1 (.sel(offset), .in_0(D[31:0]), .in_1(D[63:32]), .out(multiplexer_1_out));
  BitExtender #(.inputBits(32), .outputBits(64)) bitextender_1 (.in(multiplexer_1_out), .out(Dlw));
endmodule
