// Digital circuit project05-cg.dig as structural Verilog
module project05_cg (
  input  [4:0] PROG,
  input  CLK,
  input  EN,
  input  CLR,
  input  [63:0] ioA0,
  input  [63:0] ioA1,
  input  [63:0] ioA2,
  input  [63:0] ioA3,
  input  [63:0] ioA4,
  input  [63:0] ioA5,
  input  [63:0] ioA6,
  input  [63:0] ioA7,
  output [63:0] T0,
  output [63:0] T1,
  output [63:0] A0,
  output [63:0] A1,
  output [63:0] A2,
  output DONE,
  output [63:0] A3
);

  wire ALUOp, ALUSrcA, and_2_out, CLK_t, Load, PCBR, RFW, Store;
  wire [1:0] BROp, Msz, PCsel, WDsel;
  wire [2:0] alu_1_p4, ALUSrcB;
  wire [4:0] INUM, rd, rs1, rs2;
  wire [6:0] alu_1_p4_2;
  wire [7:0] CB0, CB1, CB2, CB3, CB4, CB5, CB6, CB7, rom_1_d, rom_1_d_2, rom_1_d_3, rom_1_d_4;
  wire [31:0] iw;
  wire [63:0] Dm, imm_B, imm_I, imm_J, imm_S, lb_decoder_1_dlb, lw_decoder_1_dlw, multiplexer_1_out,
       multiplexer_2_out, multiplexer_3_out, multiplexer_4_out, multiplexer_5_out, multiplexer_6_out,
       multiplexer_7_out, pc, PC_plus_4_s, register_file_1_rd0, register_file_1_rd1, sb_decoder_1_dsb,
       sw_decoder_1_dsw, x0, x1, x2, x3, x4, x7, x8, x9, x14, x15, x16, x17, x18, x19, x20, x21, x22, x23,
       x24, x25, x26, x27, x28, x29, x30, x31;
  wire [63:10] alu_1_p4_3;

  Multiplexer #(.Bits(64)) multiplexer_1 (
    .sel(PCBR), .in_0(PC_plus_4_s), .in_1({alu_1_p4_3, alu_1_p4_2, alu_1_p4}), .out(multiplexer_1_out));
  Multiplexer #(.Selector_Bits(2), .Bits(64)) multiplexer_2 (
    .sel(PCsel), .in_0(PC_plus_4_s), .in_1({alu_1_p4_3, alu_1_p4_2, alu_1_p4}), .in_2(multiplexer_1_out),
    .in_3({64{1'b0}}), .out(multiplexer_2_out));
  and and_1 (CLK_t, CLK, ~DONE);  // And
  Comparator #(.Bits(32)) comparator_1 (.a(iw), .b(32'hc0001073), .eq(DONE));  // open: gt, lt
  register _64bit_register (.D(multiplexer_2_out), .CLK(CLK_t), .EN(EN), .CLR(CLR), .Q(pc));
  // Probe on pc
  // Probe on iw
  // Probe on rs1
  // Probe on rs2
  // Probe on rd
  // Probe on imm_I
  // Probe on imm_J
  // Probe on imm_B
  // Probe on imm_S
  LED led_1 (.in(DONE));
  Add #(.Bits(64)) PC_plus_4 (.a(pc), .b(64'h4), .c_i(1'b0), .s(PC_plus_4_s));  // open: c_o
  // Probe on x0
  // Probe on x1
  // Probe on x2
  // Probe on x3
  // Probe on x4
  // Probe on T0
  // Probe on T1
  // Probe on x7
  instruction_memory instruction_memory_1 (.PROG(PROG), .ADDR(pc[10:2]), .IW(iw));
  // Probe on x8
  // Probe on x9
  // Probe on A0
  // Probe on A1
  // Probe on A2
  // Probe on A3
  // Probe on x14
  // Probe on x15
  Multiplexer #(.Selector_Bits(3), .Bits(64)) multiplexer_3 (
    .sel(rs1[2:0]), .in_0(ioA0), .in_1(ioA1), .in_2(ioA2), .in_3(ioA3), .in_4(ioA4), .in_5(ioA5),
    .in_6(ioA6), .in_7(ioA7), .out(multiplexer_3_out));
  // Probe on x16
  // Probe on x17
  // Probe on x18
  // Probe on x19
  // Probe on x20
  // Probe on x21
  // Probe on x22
  // Probe on x23
  // InstDecoder instdecoder_1: pin names not known; wires that end beside it: iw, WDsel, PCsel, ALUSrcB, ALUSrcA, ALUOp, RFW, BROp, Store, Load, Msz, INUM
  RegDecoder regdecoder_1 (.IW(iw), .RS1(rs1), .RS2(rs2), .RD(rd));
  ImmDecoder immdecoder_1 (.IW(iw), .imm_I(imm_I), .imm_S(imm_S), .imm_B(imm_B), .imm_J(imm_J));  // open: imm_U
  and and_2 (and_2_out, RFW, EN);
  // Probe on x24
  // Probe on x25
  // Probe on x26
  // Probe on x27
  // Probe on x28
  // Probe on x29
  // Probe on x30
  // Probe on x31
  Multiplexer #(.Selector_Bits(2), .Bits(64)) multiplexer_4 (
    .sel(WDsel), .in_0({alu_1_p4_3, alu_1_p4_2, alu_1_p4}), .in_1(PC_plus_4_s), .in_2(Dm),
    .in_3(multiplexer_3_out), .out(multiplexer_4_out));
  register_file register_file_1 (
    .RR0(rs1), .RR1(rs2), .WE(and_2_out), .WR(rd), .WD(multiplexer_4_out), .CLK(CLK_t), .CLR(CLR),
    .RD0(register_file_1_rd0), .RD1(register_file_1_rd1), .x0(x0), .x1(x1), .x2(x2), .x3(x3), .x4(x4),
    .x5(T0), .x6(T1), .x7(x7), .x8(x8), .x9(x9), .x10(A0), .x11(A1), .x12(A2), .x13(A3), .x14(x14),
    .x15(x15), .x16(x16), .x17(x17), .x18(x18), .x19(x19), .x20(x20), .x21(x21), .x22(x22), .x23(x23),
    .x24(x24), .x25(x25), .x26(x26), .x27(x27), .x28(x28), .x29(x29), .x30(x30), .x31(x31));
  ROM #(.AddrBits(5), .Bits(32)) rom_1 (.A(INUM), .sel(1'b1), .D({rom_1_d_4, rom_1_d_3, rom_1_d_2, rom_1_d}));
  BU bu_1 (.A(register_file_1_rd0), .B(register_file_1_rd1), .BRop(BROp), .BR(PCBR));
  // Probe on rom_1_d_4
  // Probe on rom_1_d_3
  // Probe on rom_1_d_2
  // Probe on rom_1_d
  Multiplexer #(.Bits(64)) multiplexer_5 (
    .sel(ALUSrcA), .in_0(register_file_1_rd0), .in_1(pc), .out(multiplexer_5_out));
  Multiplexer #(.Selector_Bits(3), .Bits(64)) multiplexer_6 (
    .sel(ALUSrcB), .in_0(register_file_1_rd1), .in_1(imm_I), .in_2(imm_J), .in_3(imm_B), .in_4(imm_S),
    .in_5({64{1'b0}}), .in_6({64{1'b0}}), .in_7({64{1'b0}}), .out(multiplexer_6_out));
  // ALU alu_1: pin names not known; wires that end beside it: multiplexer_5_out, multiplexer_6_out, ALUOp, {alu_1_p4_3, alu_1_p4_2, alu_1_p4}
  sw_decoder sw_decoder_1 (
    .offset(alu_1_p4[2]), .Dsw(sw_decoder_1_dsw), .NW(register_file_1_rd1[31:0]), .C0({CB3, CB2, CB1, CB0}),
    .C1({CB7, CB6, CB5, CB4}));
  sb_decoder sb_decoder_1 (
    .offset(alu_1_p4), .Dsb(sb_decoder_1_dsb), .NB(register_file_1_rd1[7:0]), .CB0(CB0), .CB1(CB1),
    .CB2(CB2), .CB3(CB3), .CB4(CB4), .CB5(CB5), .CB6(CB6), .CB7(CB7));
  Multiplexer #(.Selector_Bits(2), .Bits(64)) multiplexer_7 (
    .sel(Msz), .in_0(sb_decoder_1_dsb), .in_1({64{1'b0}}), .in_2(sw_decoder_1_dsw),
    .in_3(register_file_1_rd1), .out(multiplexer_7_out));
  RAMDualPort #(.AddrBits(7), .Bits(64)) DataMem (
    .A(alu_1_p4_2), .Din(multiplexer_7_out), .str(Store), .C(CLK_t), .ld(Load),
    .D({CB7, CB6, CB5, CB4, CB3, CB2, CB1, CB0}));
  lb_decoder lb_decoder_1 (.D({CB7, CB6, CB5, CB4, CB3, CB2, CB1, CB0}), .Dlb(lb_decoder_1_dlb), .offset(alu_1_p4));
  lw_decoder lw_decoder_1 (.D({CB7, CB6, CB5, CB4, CB3, CB2, CB1, CB0}), .offset(alu_1_p4[2]), .Dlw(lw_decoder_1_dlw));
  Multiplexer #(.Selector_Bits(2), .Bits(64)) multiplexer_8 (
    .sel(Msz), .in_0(lb_decoder_1_dlb), .in_1({64{1'b0}}), .in_2(lw_decoder_1_dlw),
    .in_3({CB7, CB6, CB5, CB4, CB3, CB2, CB1, CB0}), .out(Dm));

  // Other names for the same wires on the sheet: CW0[31:0] = {CB3, CB2, CB1, CB0}; CW1[31:0] = {CB7, CB6, CB5, CB4};
  //   IO_A0[63:0] = ioA0; IO_A1[63:0] = ioA1; IO_A2[63:0] = ioA2; IO_A3[63:0] = ioA3; IO_A4[63:0] = ioA4;
  //   IO_A5[63:0] = ioA5; IO_A6[63:0] = ioA6; IO_A7[63:0] = ioA7; x5[63:0] = T0; x6[63:0] = T1; x10[63:0] = A0;
  //   x11[63:0] = A1; x12[63:0] = A2; x13[63:0] = A3

  // Notes on the sheet:
  //   CLK: Hz: 20
  //   contents of rom_1 (hex, n*v repeats v):
  //   41444449,41444452,4a414c5f,4a414c52,4d554c5f,534c4c5f,534c4c49
  //   ,53524c5f,53524c49,4245515f,424e455f,424c545f,4247455f,5355425f
  //   ,414e445f,4c445f5f,4c575f5f,4c425f5f,53445f5f,53575f5f,53425f5f
  //   ,4f525f5f,4c42555f,584f525f,5352415f,4449565f
endmodule
