// Digital circuit project05.dig as structural Verilog
module project05 (
  input  [4:0] PROG,
  input  CLK,
  input  EN,
  input  CLR,
  output [63:0] T0,
  output [63:0] T1,
  output [63:0] A0,
  output [63:0] A1,
  output [63:0] A2,
  output DONE,
  output [63:0] A3
);

  wire ALUSrcA, and_2_out, CLK_t, PCBR, RFW, Store;
  wire [1:0] BROp, PCsel, WDsel;
  wire [2:0] ALUOp, ALUSrcB;
  wire [4:0] rd, rs1, rs2;
  wire [6:0] alu_1_r_2;
  wire [31:0] iw;
  wire [63:0] alu_1_r, Dram, imm_B, imm_I, imm_J, imm_S, multiplexer_1_out, multiplexer_2_out,
       multiplexer_3_out, multiplexer_4_out, multiplexer_5_out, pc, PC_plus_4_s, register_file_1_rd0,
       register_file_1_rd1, x0, x1, x2, x3, x4, x7, x8, x9, x14, x15, x16, x17, x18, x19, x20, x21, x22, x23,
       x24, x25, x26, x27, x28, x29, x30, x31;

  Multiplexer #(.Bits(64)) multiplexer_1 (
    .sel(PCBR), .in_0(PC_plus_4_s), .in_1({alu_1_r[63:10], alu_1_r_2, alu_1_r[2:0]}), .out(multiplexer_1_out));
  Multiplexer #(.Selector_Bits(2), .Bits(64)) multiplexer_2 (
    .sel(PCsel), .in_0(PC_plus_4_s), .in_1({alu_1_r[63:10], alu_1_r_2, alu_1_r[2:0]}),
    .in_2(multiplexer_1_out), .in_3({64{1'b0}}), .out(multiplexer_2_out));
  and and_1 (CLK_t, CLK, ~DONE);  // And
  Comparator #(.Bits(32)) comparator_1 (.a(iw), .b(32'hc0001073), .eq(DONE));  // open: gt, lt
  register _64bit_register (.D(multiplexer_2_out), .CLK(CLK_t), .EN(EN), .CLR(CLR), .Q(pc));
  LED led_1 (.in(DONE));
  // Probe on pc
  // Probe on iw
  // Probe on rs1
  // Probe on rs2
  // Probe on rd
  // Probe on imm_I
  Add #(.Bits(64)) PC_plus_4 (.a(pc), .b(64'h4), .c_i(1'b0), .s(PC_plus_4_s));  // open: c_o
  instruction_memory instruction_memory_1 (.PROG(PROG), .ADDR(pc[10:2]), .IW(iw));
  // Probe on x0
  // Probe on x1
  // Probe on x2
  // Probe on x3
  // Probe on x4
  // Probe on T0
  // Probe on T1
  // Probe on x7
  // Probe on x8
  // Probe on x9
  // Probe on A0
  // Probe on A1
  // Probe on A2
  // Probe on A3
  // Probe on x14
  // Probe on x15
  InstDecoder instdecoder_1 (
    .IW(iw), .WDsel(WDsel), .PCsel(PCsel), .ALUSrcB(ALUSrcB), .ALUSrcA(ALUSrcA), .ALUOp(ALUOp), .RFW(RFW),
    .BROp(BROp), .Store(Store));
  RegDecoder regdecoder_1 (.IW(iw), .RS1(rs1), .RS2(rs2), .RD(rd));
  ImmDecoder immdecoder_1 (.IW(iw), .imm_I(imm_I), .imm_S(imm_S), .imm_B(imm_B), .imm_J(imm_J));  // open: imm_U
  // Probe on x16
  // Probe on x17
  // Probe on x18
  // Probe on x19
  // Probe on x20
  // Probe on x21
  // Probe on x22
  // Probe on x23
  and and_2 (and_2_out, RFW, EN);
  // Probe on x24
  // Probe on x25
  // Probe on x26
  // Probe on x27
  // Probe on x28
  // Probe on x29
  // Probe on x30
  // Probe on x31
  Multiplexer #(.Selector_Bits(2), .Bits(64)) multiplexer_3 (
    .sel(WDsel), .in_0({alu_1_r[63:10], alu_1_r_2, alu_1_r[2:0]}), .in_1(PC_plus_4_s), .in_2(Dram),
    .in_3({64{1'b0}}), .out(multiplexer_3_out));
  register_file register_file_1 (
    .RR0(rs1), .RR1(rs2), .WE(and_2_out), .WR(rd), .WD(multiplexer_3_out), .CLK(CLK_t), .CLR(CLR),
    .RD0(register_file_1_rd0), .RD1(register_file_1_rd1), .x0(x0), .x1(x1), .x2(x2), .x3(x3), .x4(x4),
    .x5(T0), .x6(T1), .x7(x7), .x8(x8), .x9(x9), .x10(A0), .x11(A1), .x12(A2), .x13(A3), .x14(x14),
    .x15(x15), .x16(x16), .x17(x17), .x18(x18), .x19(x19), .x20(x20), .x21(x21), .x22(x22), .x23(x23),
    .x24(x24), .x25(x25), .x26(x26), .x27(x27), .x28(x28), .x29(x29), .x30(x30), .x31(x31));
  BU bu_1 (.A(register_file_1_rd0), .B(register_file_1_rd1), .BRop(BROp), .BR(PCBR));
  Multiplexer #(.Bits(64)) multiplexer_4 (
    .sel(ALUSrcA), .in_0(register_file_1_rd0), .in_1(pc), .out(multiplexer_4_out));
  Multiplexer #(.Selector_Bits(3), .Bits(64)) multiplexer_5 (
    .sel(ALUSrcB), .in_0(register_file_1_rd1), .in_1(imm_I), .in_2(imm_J), .in_3(imm_B), .in_4(imm_S),
    .in_5({64{1'b0}}), .in_6({64{1'b0}}), .in_7({64{1'b0}}), .out(multiplexer_5_out));
  ALU alu_1 (
    .A(multiplexer_4_out), .B(multiplexer_5_out), .ALUOp(ALUOp), .R({alu_1_r[63:10], alu_1_r_2, alu_1_r[2:0]}));
  RAMDualPort #(.AddrBits(7), .Bits(64)) ramdualport_1 (
    .A(alu_1_r_2), .Din(register_file_1_rd1), .str(Store), .C(CLK_t), .ld(1'b1), .D(Dram));

  // Other names for the same wires on the sheet: x5[63:0] = T0; x6[63:0] = T1; x10[63:0] = A0; x11[63:0] = A1;
  //   x12[63:0] = A2; x13[63:0] = A3
endmodule
