// Digital circuit sb-decoder.dig as structural Verilog
module sb_decoder (
  input  [2:0] offset,
  input  [7:0] NB,
  input  [7:0] CB0,
  input  [7:0] CB1,
  input  [7:0] CB2,
  input  [7:0] CB3,
  input  [7:0] CB4,
  input  [7:0] CB5,
  input  [7:0] CB6,
  input  [7:0] CB7,
  output [63:0] Dsb
);

  Multiplexer #(.Selector_Bits(3), .Bits(64)) multiplexer_1 (
    .sel(offset), .in_0({CB7, CB6, CB5, CB4, CB3, CB2, CB1, NB}),
    .in_1({CB7, CB6, CB5, CB4, CB3, CB2, NB, CB0}), .in_2({CB7, CB6, CB5, CB4, CB3, NB, CB1, CB0}),
    .in_3({CB7, CB6, CB5, CB4, NB, CB2, CB1, CB0}), .in_4({CB7, CB6, CB5, NB, CB3, CB2, CB1, CB0}),
    .in_5({CB7, CB6, NB, CB4, CB3, CB2, CB1, CB0}), .in_6({CB7, NB, CB5, CB4, CB3, CB2, CB1, CB0}),
    .in_7({NB, CB6, CB5, CB4, CB3, CB2, CB1, CB0}), .out(Dsb));
endmodule
