// Digital circuit sll.dig as structural Verilog
module sll (
  input  [6:0] opcode,
  input  [2:0] funct3,
  input  [6:0] funct7,
  output eq
);

  wire r_type_eq, sll_2_eq, sll_eq;

  Comparator #(.Bits(7)) r_type (.a(opcode), .b(7'b0110011), .eq(r_type_eq));  // open: gt, lt
  Comparator #(.Bits(3)) sll (.a(funct3), .b(3'b001), .eq(sll_eq));  // open: gt, lt
  Comparator #(.Bits(7)) sll_2 (.a(funct7), .b({7{1'b0}}), .eq(sll_2_eq));  // open: gt, lt
  and and_1 (eq, r_type_eq, sll_eq, sll_2_eq);
endmodule
