// Digital circuit slli.dig as structural Verilog
module slli (
  input  [6:0] opcode,
  input  [2:0] funct3,
  input  [6:0] funct7,
  output eq
);

  wire r_type_eq, slli_2_eq, slli_eq;

  Comparator #(.Bits(7)) r_type (.a(opcode), .b(7'b0010011), .eq(r_type_eq));  // open: gt, lt
  Comparator #(.Bits(3)) slli (.a(funct3), .b(3'b001), .eq(slli_eq));  // open: gt, lt
  Comparator #(.Bits(7)) slli_2 (.a(funct7), .b({7{1'b0}}), .eq(slli_2_eq));  // open: gt, lt
  and and_1 (eq, r_type_eq, slli_eq, slli_2_eq);
endmodule
