// Digital circuit sra.dig as structural Verilog
module sra (
  input  [6:0] opcode,
  input  [2:0] funct3,
  input  [6:0] funct7,
  output eq
);

  wire r_type_eq, sra_2_eq, sra_eq;

  Comparator #(.Bits(7)) r_type (.a(opcode), .b(7'b0110011), .eq(r_type_eq));  // open: gt, lt
  Comparator #(.Bits(3)) sra (.a(funct3), .b(3'b101), .eq(sra_eq));  // open: gt, lt
  Comparator #(.Bits(7)) sra_2 (.a(funct7), .b(7'b0100000), .eq(sra_2_eq));  // open: gt, lt
  and and_1 (eq, r_type_eq, sra_eq, sra_2_eq);
endmodule
