// Digital circuit srli.dig as structural Verilog
module srli (
  input  [6:0] opcode,
  input  [2:0] funct3,
  input  [6:0] funct7,
  output eq
);

  wire r_type_eq, srl_2_eq, srl_eq;

  Comparator #(.Bits(7)) r_type (.a(opcode), .b(7'b0010011), .eq(r_type_eq));  // open: gt, lt
  Comparator #(.Bits(3)) srl (.a(funct3), .b(3'b101), .eq(srl_eq));  // open: gt, lt
  Comparator #(.Bits(7)) srl_2 (.a(funct7), .b({7{1'b0}}), .eq(srl_2_eq));  // open: gt, lt
  and and_1 (eq, r_type_eq, srl_eq, srl_2_eq);
endmodule
