// Digital circuit sw-decoder.dig as structural Verilog
module sw_decoder (
  input  offset,
  input  [31:0] NW,
  input  [31:0] C0,
  input  [31:0] C1,
  output [63:0] Dsw
);

  Multiplexer #(.Bits(64)) multiplexer_1 (.sel(offset), .in_0({C1, NW}), .in_1({NW, C0}), .out(Dsw));
endmodule
